# Fritzing sketch RaspiShield2 (saved by Fritzing 0.9.2b)
circuit board: 8.46667cm x 5.64444cm
breadboards: 1

parts:
  Raspberry_Pi2 = Raspberry Pi B rev2
  R4 = Resistor [tolerance=±5% resistance=10k package=THT]
  R5 = Resistor [tolerance=±5% resistance=330 package=THT]
  R6 = Resistor [tolerance=±5% resistance=330 package=THT]
  L-Verde1 = female pin header, 2 pins [form="♀ (female)"]
  L-Rojo1 = female pin header, 2 pins [form="♀ (female)"]
  Boton1 = female pin header, 2 pins [form="♀ (female)"]
  A1 = USB Connectors [package=usb-a-pcb]
  B1 = USB Connectors [package=usb-a-pcb]
  C1 = USB Connectors [package=usb-a-pcb]
  D1 = USB Connectors [package=usb-a-pcb]

nets:
  3.3V: Raspberry_Pi2.3V3, Boton1.pin1, A1.VBUS, B1.VBUS, C1.VBUS, D1.VBUS
  N1: Raspberry_Pi2.GPIO_3, D1.D-
  GND: Raspberry_Pi2.GND, R4.Pin_1, L-Verde1.pin2, L-Rojo1.pin2, A1.GND, B1.GND, C1.GND, D1.GND
  N2: Raspberry_Pi2.GPIO_17, C1.D+
  N3: Raspberry_Pi2.GPIO_18, B1.D+
  N4: Raspberry_Pi2.GPIO_27, A1.D-
  N5: Raspberry_Pi2.GPIO_22, A1.D+
  N6: Raspberry_Pi2.GPIO_4, D1.D+
  N7: Raspberry_Pi2.GPIO_24, R4.Pin_0, Boton1.pin2
  N8: Raspberry_Pi2.GPIO_25, C1.D-
  N9: Raspberry_Pi2.GPIO_11, B1.D-
  N10: Raspberry_Pi2.GPIO_8, R5.Pin_1
  N11: Raspberry_Pi2.GPIO_7, R6.Pin_1
  N12: R5.Pin_0, L-Rojo1.pin1
  N13: R6.Pin_0, L-Verde1.pin1
