# Fritzing sketch sketch-PCB (saved by Fritzing 0.9.2b)
circuit board: 8.48cm x 5.37cm
breadboards: 1

parts:
  Arduino = Arduino Nano (Rev3.0)
  Bluetooth_(HC-06) = rounded female pin header, 4 pins [form="♀ (female rounded)"]
  MPU6000 = female pin header, 7 pins [form="♀ (female)"]
  MPU9250 = female pin header, 10 pins [form="♀ (female)"]
  R1 = Resistor [tolerance=±5% resistance=330 package=THT]
  R2 = Resistor [tolerance=±5% resistance=22k package=THT]
  SR-04 = female pin header, 4 pins [form="♀ (female)"]
  LineTracker = female alternating pin header, 3 pins [form="♀ (female)"]
  Pushbutton = female pin header, 2 pins [form="♀ (female)"]
  Led = female pin header, 2 pins [form="♀ (female)"]
  Fuente = Power Cell LiPo Charger/Booster
  Bateria = female pin header, 2 pins [form="♀ (female)"]

nets:
  N1: Arduino.D1/TX, Bluetooth_(HC-06).pin1
  N2: Arduino.D0/RX, Bluetooth_(HC-06).pin2
  GND: Arduino.GND, Bluetooth_(HC-06).pin3, MPU6000.pin2, MPU9250.pin2, R1.Pin_1, R2.Pin_1, Fuente.GND, Bateria.pin2
  N3: Arduino.D2, R2.Pin_0, Pushbutton.pin2
  N4: Arduino.D5, LineTracker.pin1
  N5: Arduino.D6, Led.pin1
  N6: Arduino.D7, MPU6000.pin7, MPU9250.pin9
  N7: Arduino.D8, SR-04.pin2
  N8: Arduino.D9, SR-04.pin3
  N9: Arduino.D11/MOSI, MPU6000.pin5, MPU9250.pin4
  N10: Arduino.D12/MISO, MPU6000.pin6, MPU9250.pin7
  5V: Arduino.VIN, Bluetooth_(HC-06).pin4, MPU6000.pin1, MPU9250.pin1, SR-04.pin1, LineTracker.pin2, Pushbutton.pin1, Fuente.VCC
  N11: Arduino.D13/SCK, MPU6000.pin4, MPU9250.pin3
  N12: R1.Pin_0, Led.pin2
  N13: SR-04.pin4, LineTracker.pin3
  N14: Fuente.5VIN, Bateria.pin1

notes:
  Sensorización de Laboratorio de Física, Esquema básico del dispositivo móvil, sobre Arduino Nano  con sensores y Bluetooth. ( IMUs, Tracker y ultrasonido), 1
  OHw SensoLab
  v1.0
